# Fritzing sketch Meteoclock (saved by Fritzing 0.9.3b)

parts:
  U1 = NodeMCU V1.0
  TFT1 = Color 320x240 TFT Display, ILI9341 Controller Chip
  S1 = SPST Switch [package=switche-dpdt]
  HLK-PM1 = HLK-PM01

nets:
  N1: U1.D1, TFT1.D/C
  N2: U1.D2, TFT1.CS
  N3: U1.D4, TFT1.Reset
  GND: U1.GND, TFT1.GND, HLK-PM1.-Vo
  N4: U1.D5, TFT1.SCK
  N5: U1.D6, TFT1.SDO_(MISO)
  N6: U1.D7, TFT1.SDI_(MOSI)
  VIN: U1.Vin, TFT1.VCC, S1.P, HLK-PM1.+Vo
  N7: TFT1.LED, S1.O

custom parts:
  NodeMCU V1.0: ESP8266 based NodeMCU
  Color 320x240 TFT Display, ILI9341 Controller Chip: 2.2" TFT Display with ILI9341 Controller
